// Logisim project DECODER WITH 1 BITS.circ as structural Verilog: 1 circuit, main circuit main
module main (
  input  in_1,
  output _0,
  output _1
);

  Decoder decoder_1 (.out0(_0), .out1(_1), .sel(in_1));  // open: en
endmodule
