// Logisim project DECODER WITH 2 BITS.circ as structural Verilog: 1 circuit, main circuit main
module main (
  input  [1:0] in_1,
  output _0,
  output _1,
  output _2,
  output _3
);

  Decoder #(.select(2)) decoder_1 (.out0(_0), .out1(_1), .out2(_2), .out3(_3), .sel(in_1));  // open: en
endmodule
