// Logisim project DEMUX WITH 1 BITS.circ as structural Verilog: 1 circuit, main circuit main
module main (
  input  I,
  input  S
);

  wire demultiplexer_1_out0, demultiplexer_1_out1;

  Demultiplexer demultiplexer_1 (
    .out0(demultiplexer_1_out0), .out1(demultiplexer_1_out1), .in(I), .sel(S));  // open: en
  LED I0 (.in(demultiplexer_1_out0));
  LED I1 (.in(demultiplexer_1_out1));
endmodule
