// Logisim project DEMUX WITH 2 BITS.circ as structural Verilog: 1 circuit, main circuit main
module main (
  input  I,
  input  [1:0] S0S1
);

  wire demultiplexer_1_out0, demultiplexer_1_out1, demultiplexer_1_out2, demultiplexer_1_out3;

  Demultiplexer #(.select(2)) demultiplexer_1 (
    .out0(demultiplexer_1_out0), .out1(demultiplexer_1_out1), .out2(demultiplexer_1_out2),
    .out3(demultiplexer_1_out3), .in(I), .sel(S0S1));  // open: en
  LED I0 (.in(demultiplexer_1_out0));
  LED I1 (.in(demultiplexer_1_out1));
  LED I2 (.in(demultiplexer_1_out2));
  LED I3 (.in(demultiplexer_1_out3));
endmodule
