// Logisim project DEMUX WITH 3 BITS.circ as structural Verilog: 1 circuit, main circuit main
module main (
  input  I,
  input  [2:0] S0S1S2
);

  wire demultiplexer_1_out0, demultiplexer_1_out1, demultiplexer_1_out2, demultiplexer_1_out3,
       demultiplexer_1_out4, demultiplexer_1_out5, demultiplexer_1_out6, demultiplexer_1_out7;

  Demultiplexer #(.select(3)) demultiplexer_1 (
    .out0(demultiplexer_1_out0), .out1(demultiplexer_1_out1), .out2(demultiplexer_1_out2),
    .out3(demultiplexer_1_out3), .out4(demultiplexer_1_out4), .out5(demultiplexer_1_out5),
    .out6(demultiplexer_1_out6), .out7(demultiplexer_1_out7), .in(I), .sel(S0S1S2));  // open: en
  LED I1 (.in(demultiplexer_1_out1));
  LED I2 (.in(demultiplexer_1_out2));
  LED I5 (.in(demultiplexer_1_out5));
  LED I6 (.in(demultiplexer_1_out6));
  LED I7 (.in(demultiplexer_1_out7));
  LED I0 (.in(demultiplexer_1_out0));
  LED I3 (.in(demultiplexer_1_out3));
  LED I4 (.in(demultiplexer_1_out4));
endmodule
