// Logisim project MUX WITH 1 BITS.circ as structural Verilog: 1 circuit, main circuit main
module main (
  input  i0,
  input  i1,
  input  S
);

  wire multiplexer_1_out;

  Multiplexer multiplexer_1 (.in0(i0), .in1(i1), .out(multiplexer_1_out), .sel(S));  // open: en
  LED Y (.in(multiplexer_1_out));
endmodule
