// Logisim project MUX WITH 2 BITS.circ as structural Verilog: 1 circuit, main circuit main
module main (
  input  I0,
  input  I1,
  input  I2,
  input  I3,
  input  [1:0] S0S1
);

  wire multiplexer_1_out;

  Multiplexer #(.select(2)) multiplexer_1 (
    .in0(I0), .in1(I1), .in2(I2), .in3(I3), .out(multiplexer_1_out), .sel(S0S1));  // open: en
  LED Y (.in(multiplexer_1_out));
endmodule
