// Logisim project MUX WITH FOUR DIFFERENT VARIETY.circ as structural Verilog: 1 circuit, main circuit main
module main (
  input  A,
  input  B,
  input  [1:0] in_3,
  output out_4
);

  wire adder_1_out, and_1_out, or_1_out, xor_1_out;

  and and_1 (and_1_out, A, B);
  xor xor_1 (xor_1_out, B, A);
  Adder #(.width(1)) adder_1 (.a(B), .b(A), .out(adder_1_out));  // open: cin, cout
  or or_1 (or_1_out, B, A);
  Multiplexer #(.select(2)) multiplexer_1 (
    .in0(and_1_out), .in1(or_1_out), .in2(xor_1_out), .in3(adder_1_out), .out(out_4), .sel(in_3));  // open: en
endmodule
