// Logisim project PRI WITH 1 BITS.circ as structural Verilog: 1 circuit, main circuit main
module main (
  input  _0,
  input  _1,
  input  ENABLE,
  output BINARY
);

  Priority_Encoder #(.select(1)) priority_encoder_1 (
    .in0(_0), .in1(_1), .gs(BINARY), .en_in(ENABLE));  // open: out, en_out
endmodule
