// Logisim project PRI WITH 2 BITS.circ as structural Verilog: 1 circuit, main circuit main
module main (
  input  _0,
  input  _1,
  input  _2,
  input  ENABLE,
  input  _3,
  output [1:0] BINARY,
  output out_7
);

  Priority_Encoder #(.select(2)) priority_encoder_1 (
    .in0(_0), .in1(_1), .in2(_2), .in3(_3), .out(BINARY), .gs(out_7), .en_in(ENABLE));  // open: en_out
endmodule
