// Logisim project PRI WITH 3 BITS.circ as structural Verilog: 1 circuit, main circuit main
module main (
  input  _0,
  input  _1,
  input  _2,
  input  _3,
  input  _4,
  input  _5,
  input  _6,
  input  ENABLE,
  input  _7,
  output [2:0] BINARY
);

  Priority_Encoder priority_encoder_1 (
    .in0(_0), .in1(_1), .in2(_2), .in3(_3), .in4(_4), .in5(_5), .in6(_6), .in7(_7), .out(BINARY),
    .en_in(ENABLE));  // open: gs, en_out
endmodule
